# Fritzing sketch auto_target_3servo (saved by Fritzing 0.8.7b)
breadboards: 1

parts:
  元件1 = Arduino Nano (Rev3.0) (ICSP)
  元件2 = Bluetooth Mate Silver
  R2 = Resistor [tolerance=±5% resistance=10k package=THT]
  R1 = Resistor [tolerance=±5% resistance=10k package=THT]
  J1 = Basic Servo
  微動sw1(靶1) = Pushbutton [package=THT]
  微動sw2(靶2) = Pushbutton [package=THT]
  槍聲偵測mic = Breakout Board for Electret Microphone
  R3 = Resistor [tolerance=±5% resistance=330 package=THT]
  LED1 = Super Flux LED blue [color=Blue]
  U1 = Voltage Regulator - 5V [package="TO220 [THT]"]
  C1 = Electrolytic Capacitor [capacitance=10µF voltage=20V package="100 mil [THT, electrolytic]"]
  C2 = Electrolytic Capacitor [capacitance=100µF voltage=20V package="100 mil [THT, electrolytic]"]
  J2 = Basic Servo
  R4 = Resistor [tolerance=±5% resistance=10k package=THT]
  微動SW3(靶3) = Pushbutton [package=THT]
  J3 = Basic Servo

nets:
  N1: 元件1.D1/TX, 元件2.RX_5V
  GND: 元件1.GND, 元件2.GND, R2.Pin_1, R1.Pin_0, J1.gnd, 槍聲偵測mic.GND, R3.Pin_0
  N2: 元件1.D2, 元件2.TX_5V
  N3: 元件1.D3, J1.pulse
  N4: 元件1.D4, R4.Pin_1, 微動SW3(靶3).leg0
  N5: 元件1.D5, LED1.anode
  N6: 元件1.D6, J2.pulse
  N7: 元件1.D7, R1.Pin_1, 微動sw1(靶1).leg0
  N8: 元件1.D8, R2.Pin_0, 微動sw2(靶2).leg0
  N9: 元件1.D9, J3.pulse
  12V: 元件1.VIN, U1.input_voltage, C1.+
  VCC: 元件1.5V, 元件2.VCC, 槍聲偵測mic.VCC
  N10: 元件1.A0, 槍聲偵測mic.AUD
  5V: J1.vcc, U1.output_voltage, C2.+, J2.vcc, 微動SW3(靶3).leg1, J3.vcc
  N11: 微動sw1(靶1).leg1, 微動sw2(靶2).leg1
  N12: R3.Pin_1, LED1.cathode

notes:
  8
  1
  2
  3
  4
  5
  6
  7
  數字1~8為RJ45 pin號
